# Fritzing sketch PCB sketch (saved by Fritzing 0.9.3b)

parts:
  WeMos_D1_Mini1 = WeMos D1 Mini
  R1 = Photocell (LDR) [package=THT]
  S1 = Pushbutton [package="[THT]"]
  S2 = Pushbutton [package="[THT]"]
  J1 = Basic Servo
  J2 = Power Jack [package=power_jack_combo]
  R2 = Resistor [tolerance=±5% resistance=10k package="0603 [SMD]"]
  TIP_120 = npn-Powertransistor [package="TO220 [THT]"]
  R3 = Resistor [tolerance=±5% resistance=10k package="0603 [SMD]"]

nets:
  N1: WeMos_D1_Mini1.3V3, R1.pin_0
  5V: WeMos_D1_Mini1.5V, J1.vcc, J2.PWR
  N2: WeMos_D1_Mini1.A0, R1.pin_1, R3.Pin_0
  N3: WeMos_D1_Mini1.D3, R2.Pin_0
  N4: WeMos_D1_Mini1.D4, J1.pulse
  N5: WeMos_D1_Mini1.D5, S1.Pin_1, S1.Pin_2
  N6: WeMos_D1_Mini1.D6, S2.Pin_1
  N7: WeMos_D1_Mini1.G, S1.Pin_3, S1.Pin_4, S2.Pin_3, S2.Pin_4, TIP_120.emitter, R3.Pin_1
  N8: J1.gnd, TIP_120.collector
  N9: R2.Pin_1, TIP_120.base
